# Fritzing sketch Function decoder (saved by Fritzing 1.0.3b)
circuit board: 4.15727cm x 7.20918cm
breadboards: 1

parts:
  6N137 = 6n137 Optocoupler [package="DIP (Dual Inline) [THT]"]
  J1 = Camdenboss CTB0158-2 [part_number=CTB0158-2 package=THT]
  R1 = Resistor [tolerance=±5% power=0.25W resistance=220 package=THT]
  D1 = Zener Diode [part_number=1N4732A breakdown_voltage=3.6V package="300 mil [THT]"]
  Arduino = Arduino Nano (Rev3.0) (ICSP)
  J11 = Camdenboss CTB0158-2 [part_number=CTB0158-2 package=THT]
  3 = Dagu DGServo 9g header connector (female) [package=THT]
  2 = Dagu DGServo 9g header connector (female) [package=THT]
  1 = Dagu DGServo 9g header connector (female) [package=THT]
  4 = Dagu DGServo 9g header connector (female) [package=THT]
  5 = Dagu DGServo 9g header connector (female) [package=THT]
  6 = Dagu DGServo 9g header connector (female) [package=THT]
  7 = Dagu DGServo 9g header connector (female) [package=THT]
  8 = Dagu DGServo 9g header connector (female) [package=THT]
  9 = Dagu DGServo 9g header connector (female) [package=THT]
  R3 = Resistor [tolerance=±5% power=0.25W resistance=220 package=THT]
  R2 = Resistor [tolerance=±5% power=0.25W resistance=220 package=THT]

nets:
  N1: 6N137.Vf+, R1.Pin_1, D1.cathode
  N2: 6N137.Vf-, J1.pin2, D1.anode
  GND: 6N137.GND, Arduino.GND, J11.pin2, 3.gnd, 2.gnd, 1.gnd, 4.gnd, 5.gnd, 6.gnd, 7.gnd, 8.gnd, 9.gnd
  N3: 6N137.Vo, Arduino.D2, R3.Pin_1
  N4: 6N137.Ve, R2.Pin_1
  VCC: 6N137.Vcc, Arduino.VIN, R3.Pin_0, R2.Pin_0
  N5: J1.pin1, R1.Pin_0
  N6: Arduino.D4, 1.pulse
  N7: Arduino.D5, 2.pulse
  N8: Arduino.D6, 3.pulse
  N9: Arduino.D7, 4.pulse
  N10: Arduino.D8, 5.pulse
  N11: Arduino.D9, 6.pulse
  N12: Arduino.D10, 7.pulse
  N13: Arduino.D11/MOSI, 8.pulse
  N14: Arduino.D12/MISO, 9.pulse
  VCC_2: J11.pin1, 3.Vcc, 2.Vcc, 1.Vcc, 4.Vcc, 5.Vcc, 6.Vcc, 7.Vcc, 8.Vcc, 9.Vcc

notes:
  -  +
  DCC In
  5 V=

custom parts:
  6n137 Optocoupler: 6n137 fast Optocoupler. With 8 pins on a 300mil dual inline package (DIP) footprint. Ve is strobe input. Output is inverting.
